// Logisim project Assignmenmt_1_with_ic_minimization.circ as structural Verilog: 1 circuit, main circuit main
module main (
  input  S2,
  input  S1,
  input  S0,
  input  A3,
  input  A2,
  input  A1,
  input  A0,
  input  B3,
  input  B2,
  input  B1,
  input  B0,
  output out_12,
  output out_13
);

  wire n7404_1_p5, n7404_1_p7, n7408_2_p3, n7408_2_p6, n7432_2_p2, n7432_2_p3, n7432_2_p5, n7432_2_p6,
       n7432_2_p9, n7432_2_p10, n7432_2_p11, n7432_2_p12, n7483_1_p1, n7483_1_p2, n7483_1_p3, n7483_1_p4,
       n7483_1_p9, n7483_1_p10, n7483_1_p14, n7483_1_p15, n7483_1_p16, n7483_1_p18, n7483_2_p1, n7483_2_p7,
       n7483_2_p12;

  // _7408 7408_1: pin names not known
  // _7483 7483_1: pin names not known; wires that end beside it: n7483_1_p1, n7483_1_p2, n7483_1_p3, n7483_1_p4, n7483_1_p4, n7483_1_p3, n7483_1_p2, n7483_1_p1, n7483_1_p9, n7483_1_p10, n7483_1_p10, 1'b1, 1'b1, n7483_1_p14, n7483_1_p15, n7483_1_p16, 1'b0, n7483_1_p18, 1'b0, n7483_1_p14, n7483_1_p16, n7483_1_p18, n7483_1_p15, n7483_1_p9
  // _7404 7404_1: pin names not known; wires that end beside it: A3, S2, A2, S1, n7404_1_p5, n7404_1_p5, n7404_1_p7
  // _7432 7432_1: pin names not known
  // _7408 7408_2: pin names not known; wires that end beside it: n7404_1_p7, S0, n7408_2_p3, n7404_1_p5, S1, n7408_2_p6
  // _7432 7432_2: pin names not known; wires that end beside it: A1, n7432_2_p2, n7432_2_p3, S2, n7432_2_p5, n7432_2_p6, A0, S2, n7432_2_p9, n7432_2_p10, n7432_2_p11, n7432_2_p12
  // _7483 7483_2: pin names not known; wires that end beside it: n7483_2_p1, out_12, n7432_2_p6, n7432_2_p5, out_12, n7483_2_p1, n7483_2_p7, n7408_2_p3, 1'b1, 1'b1, n7432_2_p12, n7483_2_p12, n7432_2_p11, 1'b0, out_13, 1'b0
  // _7404 7404_2: pin names not known; wires that end beside it: B3, B2, B1, n7432_2_p2, B0, n7432_2_p10, n7432_2_p2
  // _7408 7408_3: pin names not known; wires that end beside it: n7432_2_p11, n7483_2_p12, n7432_2_p2, n7404_1_p7, n7408_2_p6, n7483_2_p7, n7432_2_p3, n7408_2_p6, n7432_2_p10, n7432_2_p9

  // Notes on the sheet:
  //   Yi = S1+ B'
  //   Xi = A + s2's1B'
  //   Zi = s0s1'
  //   Cout
  //   s3
  //   x3
  //   y3
  //   z2
  //   y2
  //   x2
  //   s2
  //   z3
  //   c2
  //   c1
  //   s1
  //   s2's1
  //   y1
  //   x1
  //   z0
  //   y0
  //   X0
  //   s0
  //   B0'
  //   c0
  //   B1'
  //   B2'
  //   z1
endmodule
