// Logisim project Assignment_2_B1_G2.circ as structural Verilog
module main (
  input  [31:0] in_1,
  input  [31:0] in_2,
  output [31:0] out_3,
  output UnderFlow,
  output OverFlow
);

  wire cmp_1_x__y, cmp_1_x_y, normall_1_frac_all_zero, subtractor_1_bout;
  wire [4:0] normall_1_shift_amount;
  wire [9:0] cmp_1_difference, cmp_1_larger;
  wire [10:0] adder_1_out;
  wire [10:10] subtractor_1_out;
  wire [23:0] adder_2_out, complement_1_out_2, multiplexer_1_out, multiplexer_2_out, shifter_1_out,
       sign_1_out_3, sign_2_out_3;

  // Probe on cmp_1_difference
  Cmp cmp_1 (
    .X(in_1[30:21]), .Y(in_2[30:21]), .X__Y(cmp_1_x__y), .X_Y(cmp_1_x_y), .Difference(cmp_1_difference),
    .Larger(cmp_1_larger));  // open: out_6
  Sign sign_1 (.in_1({3'b001, in_1[20:0]}), .Sign_Bit(in_1[31]), .out_3(sign_1_out_3));
  // Probe on multiplexer_1_out
  Multiplexer #(.width(24), .enable("false")) multiplexer_1 (
    .in0(sign_1_out_3), .in1(sign_2_out_3), .out(multiplexer_1_out), .sel(cmp_1_x__y));
  // Probe on adder_1_out
  Adder #(.width(11)) adder_1 (.a(11'h2), .b({1'b0, cmp_1_larger}), .out(adder_1_out), .cin(1'b0));  // open: cout
  // Probe on shifter_1_out
  Shifter #(.width(24), .shift("lr")) shifter_1 (
    .in(multiplexer_1_out), .\dist (cmp_1_difference[4:0]), .out(shifter_1_out));
  // Probe on {subtractor_1_out[10], out_3[30:21]}
  Subtractor #(.width(11)) subtractor_1 (
    .a(adder_1_out), .b({{6{1'b0}}, normall_1_shift_amount}), .out({subtractor_1_out[10], out_3[30:21]}),
    .bin(1'b0), .bout(subtractor_1_bout));
  Sign sign_2 (.in_1({3'b001, in_2[20:0]}), .Sign_Bit(in_2[31]), .out_3(sign_2_out_3));
  Multiplexer #(.width(24), .enable("false")) multiplexer_2 (
    .in0(sign_1_out_3), .in1(sign_2_out_3), .out(multiplexer_2_out), .sel(cmp_1_x_y));
  overflow overflow_1 (
    .Exp(out_3[30:21]), .Fraction_zero(normall_1_frac_all_zero), .Carry_of_sub(subtractor_1_bout),
    .Exp_msb(subtractor_1_out[10]), .Underflow(UnderFlow), .Overflow(OverFlow));
  // Probe on multiplexer_2_out
  Adder #(.width(24)) adder_2 (.a(multiplexer_2_out), .b(shifter_1_out), .out(adder_2_out), .cin(1'b0));  // open: cout
  // Probe on adder_2_out
  complement complement_1 (.in_1(adder_2_out), .out_2(complement_1_out_2), .out_3(out_3[31]));
  // Probe on out_3[20:0]
  normall normall_1 (
    .in_1(complement_1_out_2), .Shift_amount(normall_1_shift_amount), .Truncated_frac(out_3[20:0]),
    .Frac_all_zero(normall_1_frac_all_zero));
  // Probe on normall_1_shift_amount
endmodule

module Cmp (
  input  [9:0] X,
  input  [9:0] Y,
  output X__Y,
  output X_Y,
  output [9:0] Difference,
  output out_6,
  output [9:0] Larger
);

  wire comparator_1_eq, comparator_1_gt;
  wire [9:0] multiplexer_1_out;

  Comparator #(.width(10), .mode("unsigned")) comparator_1 (
    .a(X), .b(Y), .gt(comparator_1_gt), .eq(comparator_1_eq), .lt(X_Y));
  or or_1 (X__Y, comparator_1_gt, comparator_1_eq);
  Multiplexer #(.width(10), .disabled(0), .enable("false")) multiplexer_1 (
    .in0(X), .in1(Y), .out(multiplexer_1_out), .sel(X__Y));
  Multiplexer #(.width(10), .disabled(0), .enable("false")) multiplexer_2 (.in0(X), .in1(Y), .out(Larger), .sel(X_Y));
  Subtractor #(.width(10)) subtractor_1 (.a(Larger), .b(multiplexer_1_out), .out(Difference), .bin(1'b0), .bout(out_6));

  // Notes on the sheet:
  //   X>=Y
  //   smaller
  //   larger
  //   larger - smaller
endmodule

module Sign (
  input  [23:0] in_1,
  input  Sign_Bit,
  output [23:0] out_3
);

  wire [23:0] negator_1_out;

  Negator #(.width(24)) negator_1 (.in(in_1), .out(negator_1_out));
  Multiplexer #(.width(24), .disabled(0), .enable("false")) multiplexer_1 (
    .in0(in_1), .in1(negator_1_out), .out(out_3), .sel(Sign_Bit));
endmodule

module complement (
  input  [23:0] in_1,
  output [23:0] out_2,
  output out_3
);

  wire [23:0] negator_1_out;

  Negator #(.width(24)) negator_1 (.in(in_1), .out(negator_1_out));
  Multiplexer #(.width(24), .enable("false")) multiplexer_1 (
    .in0(in_1), .in1(negator_1_out), .out(out_2), .sel(in_1[23]));

  assign out_3 = in_1[23];
endmodule

module normall (
  input  [23:0] in_1,
  output [4:0] Shift_amount,
  output [20:0] Truncated_frac,
  output Frac_all_zero
);

  wire bitfinder_1_found;
  wire [23:0] shifter_1_out;

  BitFinder #(.width(24)) bitfinder_1 (
    .in({in_1[0], in_1[1], in_1[2], in_1[3], in_1[4], in_1[5], in_1[6], in_1[7], in_1[8], in_1[9], in_1[10], in_1[11], in_1[12], in_1[13], in_1[14], in_1[15], in_1[16], in_1[17], in_1[18], in_1[19], in_1[20], in_1[21], in_1[22], 1'b0}),
    .index(Shift_amount), .found(bitfinder_1_found));
  Shifter #(.width(24)) shifter_1 (
    .in(in_1), .\dist (Shift_amount), .out({shifter_1_out[23], Truncated_frac, shifter_1_out[1:0]}));
  Subtractor #(.width(1)) subtractor_1 (
    .a(1'b1), .b(bitfinder_1_found), .out(Frac_all_zero), .bin(1'b0));  // open: bout
endmodule

module overflow (
  input  [9:0] Exp,
  input  Fraction_zero,
  input  Carry_of_sub,
  input  Exp_msb,
  output Underflow,
  output Overflow
);

  wire n7408_1_p5, n7408_1_p6, n7408_2_p2, n7408_2_p3, n7408_2_p8, n7408_2_p9, n7408_2_p12, n7408_2_p14,
       n7408_3_p4, n7408_3_p5, n7408_3_p6, n7408_3_p7, n7432_1_p5, n7432_1_p6, n7432_1_p11, n7432_1_p12,
       n7432_2_p5, n7432_2_p6, n7432_2_p10, n7432_3_p1, n7432_3_p7, n7432_3_p9;

  // _7408 7408_1: pin names not known; wires that end beside it: Exp[5], Exp[9], Exp[4], Exp[8], n7408_1_p5, n7408_1_p6, Exp[3], Exp[7], Exp[2]
  // _7432 7432_1: pin names not known; wires that end beside it: Exp[4], Exp[1], Exp[5], Exp[0], n7432_1_p5, n7432_1_p6, Exp[6], Exp[2], Exp[7], Exp[3], n7432_1_p11, n7432_1_p12
  // _7408 7408_2: pin names not known; wires that end beside it: Exp[6], n7408_2_p2, n7408_2_p3, n7408_2_p2, Exp[1], n7408_1_p5, Exp[0], n7408_2_p8, n7408_2_p9, n7408_2_p8, n7408_1_p6, n7408_2_p12, n7408_2_p3, n7408_2_p14
  // _7432 7432_2: pin names not known; wires that end beside it: n7432_1_p11, n7432_1_p12, n7432_1_p5, n7432_1_p6, n7432_2_p5, n7432_2_p6, Exp[8], n7432_2_p6, Exp[9], n7432_2_p10, n7432_2_p10
  // _7408 7408_3: pin names not known; wires that end beside it: n7408_2_p12, n7408_2_p9, n7408_2_p14, n7408_3_p4, n7408_3_p5, n7408_3_p6, n7408_3_p7
  // _7432 7432_3: pin names not known; wires that end beside it: n7432_3_p1, Exp_msb, n7432_2_p5, n7408_3_p4, n7432_3_p1, Overflow, n7432_3_p7, n7408_3_p7, n7432_3_p9, Carry_of_sub, Fraction_zero, n7432_3_p9, Underflow
  // _7404 7404_1: pin names not known; wires that end beside it: Exp_msb, n7432_3_p7, n7408_3_p5, n7408_3_p6
endmodule

module block (
  input  in_1,
  input  [9:0] in_2,
  input  [20:0] in_3,
  input  in_4,
  input  [9:0] in_5,
  input  [20:0] in_6,
  output [20:0] out_7,
  output [9:0] out_8,
  output out_9,
  output UnderFlow,
  output OverFlow
);

  main main_1 (
    .in_1({in_1, in_2, in_3}), .in_2({in_4, in_5, in_6}), .out_3({out_9, out_8, out_7}),
    .UnderFlow(UnderFlow), .OverFlow(OverFlow));
endmodule
